// Logisim project HW2.circ as structural Verilog: 11 circuits, main circuit Vertebrate
module Vertebrate (
  input  [15:0] Din,
  input  [9:0] in_2,
  input  [9:0] shift_rslt,
  input  in_4,
  output MEMLOAD,
  output [15:0] DATA_OUT,
  output [11:0] Address_Bus
);

  wire alu_1_zf, controlunit_1_armux, controlunit_1_datamux, controlunit_1_irld, controlunit_1_memld,
       controlunit_1_mux, controlunit_1_pcinc, controlunit_1_pcld, controlunit_1_pcmux, controlunit_1_regld,
       controlunit_1_zfld, controlunit_1_zfpop, zero_1_go_cu;
  wire [2:0] ir_1_r2, ir_1_r2_0, ir_1_r3;
  wire [3:0] undriven, undriven_2;
  wire [5:0] ir_1_aluop;
  wire [9:0] shifter_1_out;
  wire [11:0] adder_1_out, ir_1_dout_11_0, multiplexer_1_out, multiplexer_2_out, multiplexer_6_out,
       pc_1_addrout, regbank_1_r3;
  wire [15:0] alu_1_dout, multiplexer_3_out, multiplexer_4_out, multiplexer_5_out, regbank_1_r1,
       regbank_1_r2, regbank_1_r4, regbank_1_r5, regbank_1_r6, regbank_1_r7, regbank_1_r8, zero_1_go_mem;
  wire [15:12] multiplexer_6_out_2, regbank_1_r3_2, undriven_3;

  _7_Segment_Display u_7_segment_display_1 (.d(undriven_2[3]));  // open: g, f, a, b, e, c, dp
  _7_Segment_Display u_7_segment_display_2 (.d(undriven_2[2]));  // open: g, f, a, b, e, c, dp
  Shifter #(.width(10)) shifter_1 (.in(in_2), .\dist (undriven), .out(shifter_1_out));
  _7_Segment_Display u_7_segment_display_3 (.d(undriven_2[1]));  // open: g, f, a, b, e, c, dp
  _7_Segment_Display u_7_segment_display_4 (.d(undriven_2[0]));  // open: g, f, a, b, e, c, dp
  CONTROLUNIT controlunit_1 (
    .OPCODE(Din[15:12]), .in_3(zero_1_go_cu), .ZFpop(controlunit_1_zfpop), .datamux(controlunit_1_datamux),
    .pcmux(controlunit_1_pcmux), .PCLD(controlunit_1_pcld), .PCINC(controlunit_1_pcinc),
    .ARMUX(controlunit_1_armux), .IRLD(controlunit_1_irld), .MEMLD(controlunit_1_memld),
    .MUX(controlunit_1_mux), .ZFLD(controlunit_1_zfld), .REGLD(controlunit_1_regld));  // open: ZF, LD, INTLoad, ifRESET, ifSET, SP_minus_minus, SP_plus_plus
  Multiplexer #(.select(2), .width(12)) multiplexer_1 (
    .in1(pc_1_addrout), .in2(multiplexer_6_out), .in3(regbank_1_r3), .out(multiplexer_1_out),
    .en(controlunit_1_armux));  // open: in0, sel
  PC pc_1 (.Addrin(multiplexer_2_out), .PCINC(controlunit_1_pcinc), .PCLD(controlunit_1_pcld), .Addrout(pc_1_addrout));
  Multiplexer #(.width(12)) multiplexer_2 (
    .in0(adder_1_out), .in1(Din[11:0]), .out(multiplexer_2_out), .sel(controlunit_1_pcmux));  // open: en
  Adder #(.width(12)) adder_1 (.a(pc_1_addrout), .b(ir_1_dout_11_0), .out(adder_1_out));  // open: cin, cout
  Multiplexer #(.select(2), .width(16)) multiplexer_3 (
    .in0(multiplexer_5_out), .in1({undriven_3, pc_1_addrout}), .in2(zero_1_go_mem), .out(multiplexer_3_out),
    .en(controlunit_1_datamux));  // open: in3, sel
  REGBANK regbank_1 (
    .Din(multiplexer_4_out), .REGLD(controlunit_1_regld), .REG(ir_1_r2), .R3({regbank_1_r3_2, regbank_1_r3}),
    .R4(regbank_1_r4), .R7(regbank_1_r7), .R8(regbank_1_r8), .R1(regbank_1_r1), .R2(regbank_1_r2),
    .R5(regbank_1_r5), .R6(regbank_1_r6));
  ZERO zero_1 (
    .zfpop(controlunit_1_zfpop), .go_mem(zero_1_go_mem), .D_0(Din[0]), .ZF(alu_1_zf), .go_CU(zero_1_go_cu),
    .ZFLD(controlunit_1_zfld));
  Multiplexer #(.width(16)) multiplexer_4 (
    .in0(alu_1_dout), .in1(Din), .out(multiplexer_4_out), .sel(controlunit_1_mux));  // open: en
  Multiplexer #(.select(3), .width(16)) multiplexer_5 (
    .in0(regbank_1_r6), .in2(regbank_1_r5), .in3(regbank_1_r2), .in4(regbank_1_r1), .in5(regbank_1_r8),
    .in6(regbank_1_r7), .in7(regbank_1_r4), .out(multiplexer_5_out), .sel(ir_1_r3));  // open: in1, en
  ALU alu_1 (
    .Din1(multiplexer_5_out), .Din2({multiplexer_6_out_2, multiplexer_6_out}), .ZF(alu_1_zf),
    .Dout(alu_1_dout), .ALUOP(ir_1_aluop));
  Multiplexer #(.select(3), .width(16)) multiplexer_6 (
    .in0(regbank_1_r6), .in1(regbank_1_r5), .in2(regbank_1_r2), .in3(regbank_1_r1), .in4(regbank_1_r8),
    .in5(regbank_1_r7), .in6(regbank_1_r4), .in7({regbank_1_r3_2, regbank_1_r3}),
    .out({multiplexer_6_out_2, multiplexer_6_out}), .sel(ir_1_r2_0));  // open: en
  IR ir_1 (
    .Din_11_0(Din[11:0]), .IRLD(controlunit_1_irld), .R3(ir_1_r3), .R2(ir_1_r2), .ALUOP(ir_1_aluop),
    .R2_0(ir_1_r2_0), .Dout_11_0(ir_1_dout_11_0));  // open: CLK
endmodule

module REGBANK (
  input  [15:0] Din,
  input  REGLD,
  input  [2:0] REG,
  output [15:0] R3,
  output [15:0] R4,
  output [15:0] R7,
  output [15:0] R8,
  output [15:0] R1,
  output [15:0] R2,
  output [15:0] R5,
  output [15:0] R6
);

  wire [15:0] demultiplexer_1_out0, demultiplexer_1_out1, demultiplexer_1_out2, demultiplexer_1_out3,
       demultiplexer_1_out4, demultiplexer_1_out5, demultiplexer_1_out6, demultiplexer_1_out7;

  _16_bit_register u_16_bit_register_1 (
    .I1(demultiplexer_1_out0[0]), .I2(demultiplexer_1_out0[1]), .I3(demultiplexer_1_out0[2]),
    .I4(demultiplexer_1_out0[3]), .I5(demultiplexer_1_out0[4]), .I6(demultiplexer_1_out0[5]),
    .I7(demultiplexer_1_out0[6]), .I8(demultiplexer_1_out0[7]), .I9(demultiplexer_1_out0[8]),
    .I10(demultiplexer_1_out0[9]), .I11(demultiplexer_1_out0[10]), .I12(demultiplexer_1_out0[11]),
    .I13(demultiplexer_1_out0[12]), .I14(demultiplexer_1_out0[13]), .I15(demultiplexer_1_out0[14]),
    .I16(demultiplexer_1_out0[15]), .Q1(R1[0]), .Q2(R1[1]), .Q3(R1[2]), .Q4(R1[3]), .Q5(R1[4]), .Q6(R1[5]),
    .Q7(R1[6]), .Q8(R1[7]), .Q9(R1[8]), .Q10(R1[9]), .Q11(R1[10]), .Q12(R1[11]), .Q13(R1[12]), .Q14(R1[13]),
    .Q15(R1[14]), .Q16(R1[15]));
  _16_bit_register u_16_bit_register_2 (
    .I1(demultiplexer_1_out1[0]), .I2(demultiplexer_1_out1[1]), .I3(demultiplexer_1_out1[2]),
    .I4(demultiplexer_1_out1[3]), .I5(demultiplexer_1_out1[4]), .I6(demultiplexer_1_out1[5]),
    .I7(demultiplexer_1_out1[6]), .I8(demultiplexer_1_out1[7]), .I9(demultiplexer_1_out1[8]),
    .I10(demultiplexer_1_out1[9]), .I11(demultiplexer_1_out1[10]), .I12(demultiplexer_1_out1[11]),
    .I13(demultiplexer_1_out1[12]), .I14(demultiplexer_1_out1[13]), .I15(demultiplexer_1_out1[14]),
    .I16(demultiplexer_1_out1[15]), .Q1(R2[0]), .Q2(R2[1]), .Q3(R2[2]), .Q4(R2[3]), .Q5(R2[4]), .Q6(R2[5]),
    .Q7(R2[6]), .Q8(R2[7]), .Q9(R2[8]), .Q10(R2[9]), .Q11(R2[10]), .Q12(R2[11]), .Q13(R2[12]), .Q14(R2[13]),
    .Q15(R2[14]), .Q16(R2[15]));
  Demultiplexer #(.select(3), .width(16)) demultiplexer_1 (
    .out0(demultiplexer_1_out0), .out1(demultiplexer_1_out1), .out2(demultiplexer_1_out2),
    .out3(demultiplexer_1_out3), .out4(demultiplexer_1_out4), .out5(demultiplexer_1_out5),
    .out6(demultiplexer_1_out6), .out7(demultiplexer_1_out7), .in(Din), .sel(REG), .en(REGLD));
  _16_bit_register u_16_bit_register_3 (
    .I1(demultiplexer_1_out2[0]), .I2(demultiplexer_1_out2[1]), .I3(demultiplexer_1_out2[2]),
    .I4(demultiplexer_1_out2[3]), .I5(demultiplexer_1_out2[4]), .I6(demultiplexer_1_out2[5]),
    .I7(demultiplexer_1_out2[6]), .I8(demultiplexer_1_out2[7]), .I9(demultiplexer_1_out2[8]),
    .I10(demultiplexer_1_out2[9]), .I11(demultiplexer_1_out2[10]), .I12(demultiplexer_1_out2[11]),
    .I13(demultiplexer_1_out2[12]), .I14(demultiplexer_1_out2[13]), .I15(demultiplexer_1_out2[14]),
    .I16(demultiplexer_1_out2[15]), .Q1(R3[0]), .Q2(R3[1]), .Q3(R3[2]), .Q4(R3[3]), .Q5(R3[4]), .Q6(R3[5]),
    .Q7(R3[6]), .Q8(R3[7]), .Q9(R3[8]), .Q10(R3[9]), .Q11(R3[10]), .Q12(R3[11]), .Q13(R3[12]), .Q14(R3[13]),
    .Q15(R3[14]), .Q16(R3[15]));
  _16_bit_register u_16_bit_register_4 (
    .I1(demultiplexer_1_out3[0]), .I2(demultiplexer_1_out3[1]), .I3(demultiplexer_1_out3[2]),
    .I4(demultiplexer_1_out3[3]), .I5(demultiplexer_1_out3[4]), .I6(demultiplexer_1_out3[5]),
    .I7(demultiplexer_1_out3[6]), .I8(demultiplexer_1_out3[7]), .I9(demultiplexer_1_out3[8]),
    .I10(demultiplexer_1_out3[9]), .I11(demultiplexer_1_out3[10]), .I12(demultiplexer_1_out3[11]),
    .I13(demultiplexer_1_out3[12]), .I14(demultiplexer_1_out3[13]), .I15(demultiplexer_1_out3[14]),
    .I16(demultiplexer_1_out3[15]), .Q1(R4[0]), .Q2(R4[1]), .Q3(R4[2]), .Q4(R4[3]), .Q5(R4[4]), .Q6(R4[5]),
    .Q7(R4[6]), .Q8(R4[7]), .Q9(R4[8]), .Q10(R4[9]), .Q11(R4[10]), .Q12(R4[11]), .Q13(R4[12]), .Q14(R4[13]),
    .Q15(R4[14]), .Q16(R4[15]));
  _16_bit_register u_16_bit_register_5 (
    .I1(demultiplexer_1_out4[0]), .I2(demultiplexer_1_out4[1]), .I3(demultiplexer_1_out4[2]),
    .I4(demultiplexer_1_out4[3]), .I5(demultiplexer_1_out4[4]), .I6(demultiplexer_1_out4[5]),
    .I7(demultiplexer_1_out4[6]), .I8(demultiplexer_1_out4[7]), .I9(demultiplexer_1_out4[8]),
    .I10(demultiplexer_1_out4[9]), .I11(demultiplexer_1_out4[10]), .I12(demultiplexer_1_out4[11]),
    .I13(demultiplexer_1_out4[12]), .I14(demultiplexer_1_out4[13]), .I15(demultiplexer_1_out4[14]),
    .I16(demultiplexer_1_out4[15]), .Q1(R5[0]), .Q2(R5[1]), .Q3(R5[2]), .Q4(R5[3]), .Q5(R5[4]), .Q6(R5[5]),
    .Q7(R5[6]), .Q8(R5[7]), .Q9(R5[8]), .Q10(R5[9]), .Q11(R5[10]), .Q12(R5[11]), .Q13(R5[12]), .Q14(R5[13]),
    .Q15(R5[14]), .Q16(R5[15]));
  _16_bit_register u_16_bit_register_6 (
    .I1(demultiplexer_1_out5[0]), .I2(demultiplexer_1_out5[1]), .I3(demultiplexer_1_out5[2]),
    .I4(demultiplexer_1_out5[3]), .I5(demultiplexer_1_out5[4]), .I6(demultiplexer_1_out5[5]),
    .I7(demultiplexer_1_out5[6]), .I8(demultiplexer_1_out5[7]), .I9(demultiplexer_1_out5[8]),
    .I10(demultiplexer_1_out5[9]), .I11(demultiplexer_1_out5[10]), .I12(demultiplexer_1_out5[11]),
    .I13(demultiplexer_1_out5[12]), .I14(demultiplexer_1_out5[13]), .I15(demultiplexer_1_out5[14]),
    .I16(demultiplexer_1_out5[15]), .Q1(R6[0]), .Q2(R6[1]), .Q3(R6[2]), .Q4(R6[3]), .Q5(R6[4]), .Q6(R6[5]),
    .Q7(R6[6]), .Q8(R6[7]), .Q9(R6[8]), .Q10(R6[9]), .Q11(R6[10]), .Q12(R6[11]), .Q13(R6[12]), .Q14(R6[13]),
    .Q15(R6[14]), .Q16(R6[15]));
  _16_bit_register u_16_bit_register_7 (
    .I1(demultiplexer_1_out6[0]), .I2(demultiplexer_1_out6[1]), .I3(demultiplexer_1_out6[2]),
    .I4(demultiplexer_1_out6[3]), .I5(demultiplexer_1_out6[4]), .I6(demultiplexer_1_out6[5]),
    .I7(demultiplexer_1_out6[6]), .I8(demultiplexer_1_out6[7]), .I9(demultiplexer_1_out6[8]),
    .I10(demultiplexer_1_out6[9]), .I11(demultiplexer_1_out6[10]), .I12(demultiplexer_1_out6[11]),
    .I13(demultiplexer_1_out6[12]), .I14(demultiplexer_1_out6[13]), .I15(demultiplexer_1_out6[14]),
    .I16(demultiplexer_1_out6[15]), .Q1(R7[0]), .Q2(R7[1]), .Q3(R7[2]), .Q4(R7[3]), .Q5(R7[4]), .Q6(R7[5]),
    .Q7(R7[6]), .Q8(R7[7]), .Q9(R7[8]), .Q10(R7[9]), .Q11(R7[10]), .Q12(R7[11]), .Q13(R7[12]), .Q14(R7[13]),
    .Q15(R7[14]), .Q16(R7[15]));
  _16_bit_register u_16_bit_register_8 (
    .I1(demultiplexer_1_out7[0]), .I2(demultiplexer_1_out7[1]), .I3(demultiplexer_1_out7[2]),
    .I4(demultiplexer_1_out7[3]), .I5(demultiplexer_1_out7[4]), .I6(demultiplexer_1_out7[5]),
    .I7(demultiplexer_1_out7[6]), .I8(demultiplexer_1_out7[7]), .I9(demultiplexer_1_out7[8]),
    .I10(demultiplexer_1_out7[9]), .I11(demultiplexer_1_out7[10]), .I12(demultiplexer_1_out7[11]),
    .I13(demultiplexer_1_out7[12]), .I14(demultiplexer_1_out7[13]), .I15(demultiplexer_1_out7[14]),
    .I16(demultiplexer_1_out7[15]), .Q1(R8[0]), .Q2(R8[1]), .Q3(R8[2]), .Q4(R8[3]), .Q5(R8[4]), .Q6(R8[5]),
    .Q7(R8[6]), .Q8(R8[7]), .Q9(R8[8]), .Q10(R8[9]), .Q11(R8[10]), .Q12(R8[11]), .Q13(R8[12]), .Q14(R8[13]),
    .Q15(R8[14]), .Q16(R8[15]));
endmodule

module ALU (
  input  [15:0] Din2,
  input  [15:0] Din1,
  input  [5:0] ALUOP,
  output ZF,
  output [15:0] Dout
);

  wire [15:0] adder_1_out, adder_2_out, and_1_out, multiplexer_2_out, not_1_out, or_1_out, subtractor_1_out,
       subtractor_2_out, xor_1_out;

  assign xor_1_out = Din2 ^ Din1;  // XOR_Gate xor_1, 16 bits wide
  assign or_1_out = Din2 | Din1;  // OR_Gate or_1, 16 bits wide
  assign and_1_out = Din2 & Din1;  // AND_Gate and_1, 16 bits wide
  Subtractor #(.width(16)) subtractor_1 (.a(Din2), .b(Din1), .out(subtractor_1_out));  // open: bin, bout
  Adder #(.width(16)) adder_1 (.a(Din2), .b(Din1), .out(adder_1_out));  // open: cin, cout
  Multiplexer #(.select(3), .width(16), .enable("false")) multiplexer_1 (
    .in0(adder_1_out), .in1(subtractor_1_out), .in2(and_1_out), .in3(or_1_out), .in4(xor_1_out),
    .in7(multiplexer_2_out), .out(Dout), .sel(ALUOP[2:0]));  // open: in5, in6
  Subtractor #(.width(16)) subtractor_2 (.a(Din1), .b(16'h1), .out(subtractor_2_out));  // open: bin, bout
  Adder #(.width(16)) adder_2 (.a(Din1), .b(16'h1), .out(adder_2_out));  // open: cin, cout
  assign not_1_out = ~Din1;  // NOT_Gate not_1, 16 bits wide
  Multiplexer #(.select(3), .width(16), .enable("false")) multiplexer_2 (
    .in0(Din1), .in1(not_1_out), .in2(adder_2_out), .in3(subtractor_2_out), .out(multiplexer_2_out),
    .sel(ALUOP[5:3]));  // open: in4, in5, in6, in7
  nor u_zf (ZF, Dout[0], Dout[1], Dout[2], Dout[3], Dout[4], Dout[5], Dout[6], Dout[7], Dout[8], Dout[9], Dout[10], Dout[11], Dout[12], Dout[13], Dout[14], Dout[15]);
endmodule

module IR (
  input  [11:0] Din_11_0,
  input  CLK,
  input  IRLD,
  output [2:0] R3,
  output [2:0] R2_0,
  output [11:0] Dout_11_0,
  output [2:0] R2,
  output [5:0] ALUOP
);

  _12_bit_register u_12_bit_register_1 (
    .I1(Din_11_0[0]), .I2(Din_11_0[1]), .I3(Din_11_0[2]), .I4(Din_11_0[3]), .I5(Din_11_0[4]),
    .I6(Din_11_0[5]), .I7(Din_11_0[6]), .I8(Din_11_0[7]), .I9(Din_11_0[8]), .I10(Din_11_0[9]),
    .I11(Din_11_0[10]), .I12(Din_11_0[11]), .CLK(CLK), .IRLD(IRLD), .Q1(R2_0[0]), .Q2(R2_0[1]), .Q3(R2_0[2]),
    .Q4(R3[0]), .Q5(R3[1]), .Q6(R3[2]), .Q7(ALUOP[0]), .Q8(ALUOP[1]), .Q9(ALUOP[2]), .Q10(ALUOP[3]),
    .Q11(ALUOP[4]), .Q12(ALUOP[5]));

  assign R2 = ALUOP[2:0];
endmodule

module PC (
  input  [11:0] Addrin,
  input  PCINC,
  input  PCLD,
  output [11:0] Addrout
);

  wire [11:0] adder_1_out;

  Multiplexer #(.width(12)) multiplexer_1 (.in0(Addrin), .in1(adder_1_out), .out(Addrout), .sel(PCINC), .en(PCLD));
  Adder #(.width(12)) adder_1 (.a(Addrin), .b(12'h1), .out(adder_1_out));  // open: cin, cout
endmodule

// ZF unit
module ZERO (
  input  zfpop,
  input  D_0,
  input  ZF,
  input  ZFLD,
  output [15:0] go_mem,
  output go_CU
);

  wire and_1_out, and_2_out, and_3_out, and_4_out, not_1_out, not_2_out, or_1_out, or_2_out, s_r_ff_1_q,
       undriven, undriven_2;

  not not_1 (not_1_out, D_0);
  not not_2 (not_2_out, ZF);
  and and_1 (and_1_out, D_0, undriven);
  and and_2 (and_2_out, ZF, undriven_2);
  and and_3 (and_3_out, not_1_out, undriven);
  and and_4 (and_4_out, not_2_out, undriven_2);
  or or_1 (or_1_out, and_1_out, and_2_out);
  S_R_Flip_Flop s_r_ff_1 (.S(or_1_out), .R(or_2_out), .Q(s_r_ff_1_q));  // open: clk, Qn, preset, reset, en
  or or_2 (or_2_out, and_3_out, and_4_out);
endmodule

module CONTROLUNIT (
  input  [3:0] OPCODE,
  input  ZF,
  input  in_3,
  input  LD,
  output datamux,
  output ifSET,
  output pcmux,
  output INTLoad,
  output SP_minus_minus,
  output ifRESET,
  output SP_plus_plus,
  output ZFpop,
  output PCLD,
  output PCINC,
  output ARMUX,
  output MEMLD,
  output MUX,
  output ZFLD,
  output REGLD,
  output IRLD
);

  wire not_1_out, not_2_out, not_3_out;
  wire [0:0] and_1_out;
  wire [3:0] multiplexer_1_out, multiplexer_2_out, n4_bit_register_1_q1;
  wire [7:1] rom_1_data;

  and and_1 (and_1_out[0], not_2_out, not_3_out, OPCODE[2], not_1_out);
  not not_1 (not_1_out, OPCODE[3]);
  not not_2 (not_2_out, OPCODE[0]);
  not not_3 (not_3_out, OPCODE[1]);
  Multiplexer #(.select(2), .width(4)) multiplexer_1 (
    .in0(OPCODE), .in1(OPCODE), .in2(4'b0000), .in3(4'b0101), .out(multiplexer_1_out),
    .sel({ZF, and_1_out[0]}));  // open: en
  _4_bit_register u_4_bit_register_1 (
    .I1(multiplexer_2_out[0]), .I2(multiplexer_2_out[1]), .I3(multiplexer_2_out[2]),
    .I4(multiplexer_2_out[3]), .in_1(in_3), .Q1(n4_bit_register_1_q1[0]), .Q2(n4_bit_register_1_q1[1]),
    .Q3(n4_bit_register_1_q1[2]), .Q4(n4_bit_register_1_q1[3]), .LD(LD));
  Multiplexer #(.width(4), .enable("false")) multiplexer_2 (
    .in0(4'b0000), .in1(multiplexer_1_out), .out(multiplexer_2_out), .sel(INTLoad));
  ROM #(.addrWidth(4), .dataWidth(16)) rom_1 (
    .addr(n4_bit_register_1_q1),
    .data({IRLD, MEMLD, MUX, ZFLD, REGLD, ARMUX, PCINC, PCLD, rom_1_data[7:6], pcmux, datamux, rom_1_data[3:1], INTLoad}));  // open: sel

  // Notes on the sheet:
  //   contents of rom_1 (hex, n*v repeats v):
  //   141 54 34 22 0 80 0 18 5*0 11
endmodule

module _16_bit_register (
  input  I1,
  input  I2,
  input  I3,
  input  I4,
  input  I5,
  input  I6,
  input  I7,
  input  I8,
  input  I9,
  input  I10,
  input  I11,
  input  I12,
  input  I13,
  input  I14,
  input  I15,
  input  I16,
  output Q1,
  output Q2,
  output Q3,
  output Q4,
  output Q5,
  output Q6,
  output Q7,
  output Q8,
  output Q9,
  output Q10,
  output Q11,
  output Q12,
  output Q13,
  output Q14,
  output Q15,
  output Q16
);

  wire clock_1_out, not_1_out, not_2_out, not_3_out, not_4_out, not_5_out, not_6_out, not_7_out, not_8_out,
       not_9_out, not_10_out, not_11_out, not_12_out, not_13_out, not_14_out, not_15_out, not_16_out;

  Clock clock_1 (.out(clock_1_out));
  not not_1 (not_1_out, I1);
  S_R_Flip_Flop s_r_ff_1 (.S(I1), .clk(clock_1_out), .R(not_1_out), .Q(Q1));  // open: Qn, preset, reset, en
  not not_2 (not_2_out, I2);
  S_R_Flip_Flop s_r_ff_2 (.S(I2), .clk(clock_1_out), .R(not_2_out), .Q(Q2));  // open: Qn, preset, reset, en
  not not_3 (not_3_out, I3);
  S_R_Flip_Flop s_r_ff_3 (.S(I3), .clk(clock_1_out), .R(not_3_out), .Q(Q3));  // open: Qn, preset, reset, en
  S_R_Flip_Flop s_r_ff_4 (.S(I4), .clk(clock_1_out), .R(not_4_out), .Q(Q4));  // open: Qn, preset, reset, en
  not not_4 (not_4_out, I4);
  not not_5 (not_5_out, I5);
  S_R_Flip_Flop s_r_ff_5 (.S(I5), .clk(clock_1_out), .R(not_5_out), .Q(Q5));  // open: Qn, preset, reset, en
  not not_6 (not_6_out, I6);
  S_R_Flip_Flop s_r_ff_6 (.S(I6), .clk(clock_1_out), .R(not_6_out), .Q(Q6));  // open: Qn, preset, reset, en
  not not_7 (not_7_out, I7);
  S_R_Flip_Flop s_r_ff_7 (.S(I7), .clk(clock_1_out), .R(not_7_out), .Q(Q7));  // open: Qn, preset, reset, en
  not not_8 (not_8_out, I8);
  S_R_Flip_Flop s_r_ff_8 (.S(I8), .clk(clock_1_out), .R(not_8_out), .Q(Q8));  // open: Qn, preset, reset, en
  not not_9 (not_9_out, I9);
  S_R_Flip_Flop s_r_ff_9 (.S(I9), .clk(clock_1_out), .R(not_9_out), .Q(Q9));  // open: Qn, preset, reset, en
  not not_10 (not_10_out, I10);
  S_R_Flip_Flop s_r_ff_10 (.S(I10), .clk(clock_1_out), .R(not_10_out), .Q(Q10));  // open: Qn, preset, reset, en
  not not_11 (not_11_out, I11);
  S_R_Flip_Flop s_r_ff_11 (.S(I11), .clk(clock_1_out), .R(not_11_out), .Q(Q11));  // open: Qn, preset, reset, en
  not not_12 (not_12_out, I12);
  S_R_Flip_Flop s_r_ff_12 (.S(I12), .clk(clock_1_out), .R(not_12_out), .Q(Q12));  // open: Qn, preset, reset, en
  not not_13 (not_13_out, I13);
  S_R_Flip_Flop s_r_ff_13 (.S(I13), .clk(clock_1_out), .R(not_13_out), .Q(Q13));  // open: Qn, preset, reset, en
  not not_14 (not_14_out, I14);
  S_R_Flip_Flop s_r_ff_14 (.S(I14), .clk(clock_1_out), .R(not_14_out), .Q(Q14));  // open: Qn, preset, reset, en
  not not_15 (not_15_out, I15);
  S_R_Flip_Flop s_r_ff_15 (.S(I15), .clk(clock_1_out), .R(not_15_out), .Q(Q15));  // open: Qn, preset, reset, en
  not not_16 (not_16_out, I16);
  S_R_Flip_Flop s_r_ff_16 (.S(I16), .clk(clock_1_out), .R(not_16_out), .Q(Q16));  // open: Qn, preset, reset, en
endmodule

module _12_bit_register (
  input  I1,
  input  I2,
  input  I3,
  input  I4,
  input  I5,
  input  I6,
  input  I7,
  input  I8,
  input  I9,
  input  I10,
  input  I11,
  input  I12,
  input  CLK,
  input  IRLD,
  output Q1,
  output Q2,
  output Q3,
  output Q4,
  output Q5,
  output Q6,
  output Q7,
  output Q8,
  output Q9,
  output Q10,
  output Q11,
  output Q12
);

  wire not_1_out, not_2_out, not_3_out, not_4_out, not_5_out, not_6_out, not_7_out, not_8_out, not_9_out,
       not_10_out, not_11_out, not_12_out;

  not not_1 (not_1_out, I1);
  S_R_Flip_Flop s_r_ff_1 (.S(I1), .clk(CLK), .R(not_1_out), .Q(Q1), .en(IRLD));  // open: Qn, preset, reset
  not not_2 (not_2_out, I2);
  S_R_Flip_Flop s_r_ff_2 (.S(I2), .clk(CLK), .R(not_2_out), .Q(Q2), .en(IRLD));  // open: Qn, preset, reset
  not not_3 (not_3_out, I3);
  S_R_Flip_Flop s_r_ff_3 (.S(I3), .clk(CLK), .R(not_3_out), .Q(Q3), .en(IRLD));  // open: Qn, preset, reset
  S_R_Flip_Flop s_r_ff_4 (.S(I4), .clk(CLK), .R(not_4_out), .Q(Q4), .en(IRLD));  // open: Qn, preset, reset
  not not_4 (not_4_out, I4);
  not not_5 (not_5_out, I5);
  S_R_Flip_Flop s_r_ff_5 (.S(I5), .clk(CLK), .R(not_5_out), .Q(Q5), .en(IRLD));  // open: Qn, preset, reset
  not not_6 (not_6_out, I6);
  S_R_Flip_Flop s_r_ff_6 (.S(I6), .clk(CLK), .R(not_6_out), .Q(Q6), .en(IRLD));  // open: Qn, preset, reset
  not not_7 (not_7_out, I7);
  S_R_Flip_Flop s_r_ff_7 (.S(I7), .clk(CLK), .R(not_7_out), .Q(Q7), .en(IRLD));  // open: Qn, preset, reset
  not not_8 (not_8_out, I8);
  S_R_Flip_Flop s_r_ff_8 (.S(I8), .clk(CLK), .R(not_8_out), .Q(Q8), .en(IRLD));  // open: Qn, preset, reset
  not not_9 (not_9_out, I9);
  S_R_Flip_Flop s_r_ff_9 (.S(I9), .clk(CLK), .R(not_9_out), .Q(Q9), .en(IRLD));  // open: Qn, preset, reset
  not not_10 (not_10_out, I10);
  S_R_Flip_Flop s_r_ff_10 (.S(I10), .clk(CLK), .R(not_10_out), .Q(Q10), .en(IRLD));  // open: Qn, preset, reset
  not not_11 (not_11_out, I11);
  S_R_Flip_Flop s_r_ff_11 (.S(I11), .clk(CLK), .R(not_11_out), .Q(Q11), .en(IRLD));  // open: Qn, preset, reset
  not not_12 (not_12_out, I12);
  S_R_Flip_Flop s_r_ff_12 (.S(I12), .clk(CLK), .R(not_12_out), .Q(Q12), .en(IRLD));  // open: Qn, preset, reset
endmodule

module _4_bit_register (
  input  in_1,
  input  I1,
  input  I2,
  input  I3,
  input  I4,
  input  LD,
  output Q1,
  output Q2,
  output Q3,
  output Q4
);

  wire and_1_out, CLK_out, not_1_out, not_2_out, not_3_out, not_4_out;

  Clock CLK (.out(CLK_out));
  and and_1 (and_1_out, in_1, CLK_out);
  not not_1 (not_1_out, I1);
  S_R_Flip_Flop s_r_ff_1 (.S(I1), .clk(and_1_out), .R(not_1_out), .Q(Q1), .en(LD));  // open: Qn, preset, reset
  not not_2 (not_2_out, I2);
  S_R_Flip_Flop s_r_ff_2 (.S(I2), .clk(and_1_out), .R(not_2_out), .Q(Q2), .en(LD));  // open: Qn, preset, reset
  not not_3 (not_3_out, I3);
  S_R_Flip_Flop s_r_ff_3 (.S(I3), .clk(and_1_out), .R(not_3_out), .Q(Q3), .en(LD));  // open: Qn, preset, reset
  not not_4 (not_4_out, I4);
  S_R_Flip_Flop s_r_ff_4 (.S(I4), .clk(and_1_out), .R(not_4_out), .Q(Q4), .en(LD));  // open: Qn, preset, reset
endmodule

module _1_bit_register (
  input  in_1,
  input  I1,
  input  CLK,
  output Q1
);

  wire and_1_out, not_1_out;

  and and_1 (and_1_out, in_1, CLK);
  not not_1 (not_1_out, I1);
  S_R_Flip_Flop s_r_ff_1 (.S(I1), .clk(and_1_out), .R(not_1_out), .Q(Q1));  // open: Qn, preset, reset, en
endmodule
